// Digital circuit ULA.dig as structural Verilog
module ULA (
  input  [3:0] Reg,
  input  [3:0] Acc,
  input  aluOP,
  output [3:0] R
);

  wire [3:0] add_1_s, sub_1_s;

  Add #(.Bits(4)) add_1 (.a(Reg), .b(Acc), .c_i(1'b0), .s(add_1_s));  // open: c_o
  Sub #(.Bits(4)) sub_1 (.a(Reg), .b(Acc), .c_i(1'b0), .s(sub_1_s));  // open: c_o
  Multiplexer #(.Bits(4)) multiplexer_1 (.sel(aluOP), .in_0(add_1_s), .in_1(sub_1_s), .out(R));
endmodule
