// Digital circuit Unidade de controle.dig as structural Verilog
module Unidade_de_controle (
  input  [15:0] ROM,
  output enACC,
  output enREG,
  output aluOP,
  output accSlct
);


  assign accSlct = 1'b1;
  assign aluOP = 1'b1;
  assign enACC = 1'b1;
  assign enREG = 1'b1;
endmodule
