// Digital circuit intel4004.dig as structural Verilog
module intel4004 (
  input  Clock,
  input  in_2,
  input  in_3,
  input  in_4,
  input  in_5
);

  wire [3:0] ACC_q, Banco_de_Reg_da, multiplexer_1_out, ROM_d_2, ULA_r;
  wire [11:0] PC__plus__4_s, PC_q;
  wire [15:0] ROM_d;

  Register #(.Bits(12), .Initial(0)) PC (.D(PC__plus__4_s), .C(Clock), .en(1'b1), .Q(PC_q));
  Add #(.Bits(12)) PC__plus__4 (.a(12'h4), .b(PC_q), .c_i(1'b0), .s(PC__plus__4_s));  // open: c_o
  ROM #(.WordSize(8), .AddrBits(12), .Contents("D1 60 61 D3 62 81 60 61 72 A2 05 F0 00 00 00 00"), .AddressSize(4), .Bits(16)) ROM (
    .A(PC_q), .sel(1'b1), .D({ROM_d[15:12], ROM_d_2, ROM_d[7:0]}));
  Multiplexer #(.Bits(4)) multiplexer_1 (.sel(in_2), .in_0(ROM_d_2), .in_1(ULA_r), .out(multiplexer_1_out));
  // Unidade_de_controle unidade_de_controle_1: pin names not known; wires that end beside it: {ROM_d[15:12], ROM_d_2, ROM_d[7:0]}, {ROM_d[15:12], ROM_d_2, ROM_d[7:0]}
  // Probe on multiplexer_1_out
  Register #(.Bits(4), .Initial(0)) ACC (.D(multiplexer_1_out), .C(Clock), .en(in_3), .Q(ACC_q));
  // Probe on ACC_q
  ULA ULA (.Reg(Banco_de_Reg_da), .Acc(ACC_q), .R(ULA_r), .aluOP(in_4));
  RegisterFile #(.AddrBits(4), .Bits(4)) Banco_de_Reg (
    .Din(ACC_q), .we(in_5), .Rw(ROM_d_2), .C(Clock), .Ra(ROM_d_2), .Rb(4'b0001), .Da(Banco_de_Reg_da));  // open: Db
  // Probe on Banco_de_Reg_da

  // Notes on the sheet:
  //   Clock: Hz: 1Hz
  //   contents of ROM (hex, n*v repeats v):
  //   4*0,100,0,0,0,300,0,0,0,400,0,0,0,300,400,7*0,200
endmodule
